// Digital circuit ALU6Bit.dig as structural Verilog
module ALU6Bit (
  input  [5:0] X_5_0,
  input  [5:0] Y_5_0,
  input  [1:0] OP_1_0,
  output CF,
  output [5:0] R_5_0,
  output SF
);

  wire [5:0] and6bit_1_and_5_0, fa6bit_1_s_5_0, ror6bit_1_ror_5_0;

  AND6Bit and6bit_1 (.X_5_0(X_5_0), .Y_5_0(Y_5_0), .AND_5_0(and6bit_1_and_5_0));
  FA6Bit fa6bit_1 (.S_5_0(fa6bit_1_s_5_0), .C(CF), .X_5_0(X_5_0), .Y_5_0(Y_5_0));
  ROR6Bit ror6bit_1 (.ROR_5_0(ror6bit_1_ror_5_0), .X_5_0(X_5_0), .Sel_5_0(Y_5_0));
  Multiplexer #(.Selector_Bits(2), .Bits(6)) multiplexer_1 (
    .sel(OP_1_0), .in_0(and6bit_1_and_5_0), .in_1(fa6bit_1_s_5_0), .in_2(ror6bit_1_ror_5_0),
    .in_3({6{1'b0}}), .out(R_5_0));

  assign SF = R_5_0[0];

  // Other names for the same wires on the sheet: OP[1:0] = OP_1_0; X[5:0] = X_5_0; Y[5:0] = Y_5_0
endmodule
